// Logisim project oblArqui.circ as structural Verilog
module main (
);

  wire clock_1_out, decoder_1_out1, decoder_1_out2, decoder_1_out3, decoder_1_out4, decoder_1_out5;
  wire [2:0] undriven;
  wire [7:0] shift_register_1_q7, shift_register_2_q7, shift_register_3_q7, shift_register_4_q7,
       shift_register_5_q7;

  J_K_Flip_Flop j_k_ff_1 ();  // open: J, K, clk, Q, Qn, preset, reset
  Decoder #(.select(3)) decoder_1 (
    .out1(decoder_1_out1), .out2(decoder_1_out2), .out3(decoder_1_out3), .out4(decoder_1_out4),
    .out5(decoder_1_out5), .sel(undriven));  // open: out0, out6, out7, en
  Random #(.width(3)) random_1 ();  // open: clk, next, out, clr
  Clock clock_1 (.out(clock_1_out));
  Shift_Register shift_register_1 (
    .in(decoder_1_out1), .clk(clock_1_out), .q0(shift_register_1_q7[7]), .q1(shift_register_1_q7[6]),
    .q2(shift_register_1_q7[5]), .q3(shift_register_1_q7[4]), .q4(shift_register_1_q7[3]),
    .q5(shift_register_1_q7[2]), .q6(shift_register_1_q7[1]), .q7(shift_register_1_q7[0]));  // open: shift, out, load, clr, d0, d1, d2, d3, d4, d5, d6, d7
  Shift_Register shift_register_2 (
    .in(decoder_1_out2), .clk(clock_1_out), .q0(shift_register_2_q7[7]), .q1(shift_register_2_q7[6]),
    .q2(shift_register_2_q7[5]), .q3(shift_register_2_q7[4]), .q4(shift_register_2_q7[3]),
    .q5(shift_register_2_q7[2]), .q6(shift_register_2_q7[1]), .q7(shift_register_2_q7[0]));  // open: shift, out, load, clr, d0, d1, d2, d3, d4, d5, d6, d7
  Shift_Register shift_register_3 (
    .in(decoder_1_out3), .clk(clock_1_out), .q0(shift_register_3_q7[7]), .q1(shift_register_3_q7[6]),
    .q2(shift_register_3_q7[5]), .q3(shift_register_3_q7[4]), .q4(shift_register_3_q7[3]),
    .q5(shift_register_3_q7[2]), .q6(shift_register_3_q7[1]), .q7(shift_register_3_q7[0]));  // open: shift, out, load, clr, d0, d1, d2, d3, d4, d5, d6, d7
  Shift_Register shift_register_4 (
    .in(decoder_1_out4), .clk(clock_1_out), .q0(shift_register_4_q7[7]), .q1(shift_register_4_q7[6]),
    .q2(shift_register_4_q7[5]), .q3(shift_register_4_q7[4]), .q4(shift_register_4_q7[3]),
    .q5(shift_register_4_q7[2]), .q6(shift_register_4_q7[1]), .q7(shift_register_4_q7[0]));  // open: shift, out, load, clr, d0, d1, d2, d3, d4, d5, d6, d7
  Shift_Register shift_register_5 (
    .in(decoder_1_out5), .clk(clock_1_out), .q0(shift_register_5_q7[7]), .q1(shift_register_5_q7[6]),
    .q2(shift_register_5_q7[5]), .q3(shift_register_5_q7[4]), .q4(shift_register_5_q7[3]),
    .q5(shift_register_5_q7[2]), .q6(shift_register_5_q7[1]), .q7(shift_register_5_q7[0]));  // open: shift, out, load, clr, d0, d1, d2, d3, d4, d5, d6, d7
  DotMatrix #(.matrixrows(1)) dotmatrix_1 (
    .col0(decoder_1_out1), .col1(decoder_1_out2), .col2(decoder_1_out3), .col3(decoder_1_out4),
    .col4(decoder_1_out5));
  DotMatrix #(.matrixrows(8)) dotmatrix_2 (
    .col0(shift_register_1_q7), .col1(shift_register_2_q7), .col2(shift_register_3_q7),
    .col3(shift_register_4_q7), .col4(shift_register_5_q7));
  Button button_1 ();  // open: out
endmodule
